# Fritzing sketch 7segments (saved by Fritzing 0.9.2b)
breadboards: 1

parts:
  Raspberry_Pi_B_rev2 = Raspberry Pi B rev2
  U1 = 7-SEGMENT-DISPLAY [package=7-segment-display]  # not connected
  U2 = 74HC595 [package="DIP16 [THT]"]  # not connected
  R1 = Resistor [tolerance=±5% resistance=220 package=THT]

nets:
  N1: Raspberry_Pi_B_rev2.GND, R1.Pin_0
