# Fritzing sketch 7segments2 (saved by Fritzing 0.9.2b)
breadboards: 1

parts:
  U1 = 7-SEGMENT-DISPLAY [package=7-segment-display]
  U2 = 74HC595 [package="DIP16 [THT]"]
  part = Raspberry Pi rev2  # not connected
  Raspberry_Pi_rev1 = Raspberry Pi B rev2
  R1 = Resistor [tolerance=±5% resistance=220 package=THT]

nets:
  N1: U1.E, U2.Q6
  N2: U1.D, U2.Q4
  N3: U1.G1, U2.Q3
  N4: U1.C, R1.Pin_0
  N5: U1.DP, U2.Q2
  N6: U1.B, U2.Q7
  N7: U1.A, U2.Q1
  N8: U1.G2, U2.Q0
  N9: U1.G, U2.Q5
  GND: U2.GND, U2.OE, Raspberry_Pi_rev1.GND, R1.Pin_1
  N10: U2.MR, Raspberry_Pi_rev1.GPIO_25
  N11: U2.SH_CP, Raspberry_Pi_rev1.GPIO_23
  N12: U2.ST_CP, Raspberry_Pi_rev1.GPIO_24
  N13: U2.DS, Raspberry_Pi_rev1.GPIO_18
  VCC: U2.VCC, Raspberry_Pi_rev1.5V
