# Fritzing sketch schema (saved by Fritzing 0.9.2b)
breadboards: 1

parts:
  Composant1 = Triple Axis Accelerometer Breakout - ADXL345
  Raspberry_Pi1 = Raspberry Pi 2
  LED8 = smd LED [color="Red (633nm)" package="0603 [SMD]"]
  LED9 = smd LED [color="Red (633nm)" package="0603 [SMD]"]
  LED10 = smd LED [color="Red (633nm)" package="0603 [SMD]"]
  LED11 = smd LED [color="Red (633nm)" package="0603 [SMD]"]
  R1 = Resistor [tolerance=±5% resistance=220 package="1206 [SMD]"]

nets:
  GND: Composant1.GND, Composant1.SDO, Raspberry_Pi1.GND, R1.Pin_0
  VCC: Composant1.VCC, Composant1.CS, Raspberry_Pi1.3v3
  N1: Composant1.SDA, Raspberry_Pi1.GPIO2
  N2: Composant1.SCL, Raspberry_Pi1.GPIO3
  N3: Raspberry_Pi1.GPIO21, LED9.anode
  N4: Raspberry_Pi1.GPIO20, LED8.anode
  N5: Raspberry_Pi1.GPIO16, LED11.anode
  N6: Raspberry_Pi1.GPIO12, LED10.anode
  N7: LED8.cathode, LED9.cathode, LED10.cathode, LED11.cathode, R1.Pin_1
