# Fritzing sketch led (saved by Fritzing 0.9.2b)
breadboards: 1

parts:
  Raspberry_Pi1 = Raspberry Pi 2
  LED1 = smd LED [color="Red (633nm)" package="1206 [SMD]"]
  R1 = Resistor [tolerance=±5% resistance=1k package=THT]

nets:
  N1: Raspberry_Pi1.GPIO21, LED1.anode
  N2: Raspberry_Pi1.GND, R1.Pin_1
  N3: LED1.cathode, R1.Pin_0
